// Logisim project PipelinedMipsGiven.circ as structural Verilog: 12 circuits, main circuit main
module main (
);

  wire alu_1_zero, and_1_out, Clock, EX_MEME_zero_2, EX_Squash, forward_unit_1_fwd_dm, MEM_Squash, WB_Squash;
  wire [1:0] forward_unit_1_the_output_for_s, forward_unit_1_the_output_for_t;
  wire [2:0] EX_MEME_mem_cntl_2, EX_MEME_wb_cntl_2, ID_EX_ex_cntl_2, ID_EX_ex_cntl_2_2, ID_EX_mem_cntl_2,
       ID_EX_wb_cntl_2, M, MEM_WB_wb_2, WB;
  wire [4:0] controlled_buffer_1_out, D_reg,
       EX_MEME_the_register_in_which_we_will_write__ie__the_destination_2, ID_EX_d_addr_2, ID_EX_s_addr_2,
       ID_EX_shamt_2, ID_EX_t_addr_2, MEM_WB_register_destination_2, multiplexer_6_out, S_reg, shamt, T_reg;
  wire [5:0] EX, funct, opcode;
  wire [31:0] adder_2_out, alu_1_aluresult, Branch_Target, D_PCplus4, E_imm, E_PCplus4, EX_MEME_alu_out_2,
       EX_MEME_mem_data_to_write_2, EX_MEME_pc_2, ID_EX_immediate_2, ID_EX_reg_d1_2, ID_EX_reg_d2_2,
       immediate, IR, MEM_WB_alu_out_2, MEM_WB_goddamn_ram_data_2, MEM_WB_pc_2, multiplexer_1_out,
       multiplexer_2_out, multiplexer_3_out, multiplexer_4_out, multiplexer_5_out, multiplexer_7_out, PC,
       PCplus4, ram_1_data, regfile_1_rddata1, regfile_1_rddata2, rom_1_data, shifter_1_out;

  Multiplexer #(.width(32), .enable("false")) multiplexer_1 (
    .in0(PCplus4), .in1(Branch_Target), .out(multiplexer_1_out), .sel(and_1_out));
  Register #(.width(32)) u_PC (.D(multiplexer_1_out), .Q(PC), .clk(Clock));  // open: en, clr
  Clock clock_1 (.out(Clock));
  Adder #(.width(32)) adder_1 (.a(PC), .b(32'h4), .out(PCplus4));  // open: cin, cout
  ROM #(.dataWidth(32)) rom_1 (.addr(PC[9:2]), .data(rom_1_data));  // open: sel
  IF_ID if_id_1 (.Clock(Clock), .PCplus4(PCplus4), .Instruction(rom_1_data), .PCplus4_2(D_PCplus4), .Instruction_2(IR));
  Instruction_Splitter instruction_splitter_1 (
    .Instruction(IR), .immediate(immediate), .funct(funct), .shamt(shamt), .D_reg(D_reg), .T_reg(T_reg),
    .S_reg(S_reg), .opcode(opcode));
  RegFile regfile_1 (
    .WrAddr(MEM_WB_register_destination_2), .WrData(multiplexer_7_out), .WrReg(MEM_WB_wb_2[2]),
    .RdAddr1(S_reg), .RdAddr2(T_reg), .RdData1(regfile_1_rddata1), .RdData2(regfile_1_rddata2), .Clock(Clock));
  control control_1 (
    .Funct(funct), .Opcode(opcode), .Ex(EX), .Mem(M), .WB(WB), .Ex_Squanch(EX_Squash),
    .Mem_Squanch(MEM_Squash), .WB_Squanch(WB_Squash), .Clock(Clock));
  ID_EX ID_EX (
    .EX_cntl(EX), .MEM_cntl(M), .WB_cntl(WB), .PC_plus_4(D_PCplus4), .Reg_D1(regfile_1_rddata1),
    .Reg_D2(regfile_1_rddata2), .immediate(immediate), .D_addr(D_reg), .T_addr(T_reg), .Clock(Clock),
    .Squash(EX_Squash), .EX_cntl_2({ID_EX_ex_cntl_2_2, ID_EX_ex_cntl_2}), .MEM_cntl_2(ID_EX_mem_cntl_2),
    .WB_cntl_2(ID_EX_wb_cntl_2), .PC_plus_4_2(E_PCplus4), .Reg_D1_2(ID_EX_reg_d1_2),
    .Reg_D2_2(ID_EX_reg_d2_2), .immediate_2(ID_EX_immediate_2), .D_addr_2(ID_EX_d_addr_2),
    .T_addr_2(ID_EX_t_addr_2), .Shamt(shamt), .Shamt_2(ID_EX_shamt_2), .S_addr(S_reg),
    .S_addr_2(ID_EX_s_addr_2));
  Multiplexer #(.select(2), .width(32), .enable("false")) multiplexer_2 (
    .in0(ID_EX_reg_d2_2), .in1(EX_MEME_alu_out_2), .in2(multiplexer_7_out), .in3(multiplexer_7_out),
    .out(multiplexer_2_out), .sel(forward_unit_1_the_output_for_t));
  Multiplexer #(.width(32), .enable("false")) multiplexer_3 (
    .in0(multiplexer_2_out), .in1(ID_EX_immediate_2), .out(multiplexer_3_out), .sel(ID_EX_ex_cntl_2[2]));
  assign controlled_buffer_1_out = ID_EX_ex_cntl_2[1] ? ID_EX_shamt_2 : 5'bz;  // Controlled_Buffer controlled_buffer_1
  Multiplexer #(.select(2), .width(32), .enable("false")) multiplexer_4 (
    .in0(ID_EX_reg_d1_2), .in1(EX_MEME_alu_out_2), .in2(multiplexer_7_out), .in3(multiplexer_7_out),
    .out(multiplexer_4_out), .sel(forward_unit_1_the_output_for_s));
  ALU alu_1 (
    .ALUCtl(ID_EX_ex_cntl_2_2), .A(multiplexer_4_out), .B(multiplexer_3_out), .ALUResult(alu_1_aluresult),
    .Zero(alu_1_zero), .Shamt(controlled_buffer_1_out));  // open: Overflow
  Multiplexer #(.width(32), .enable("false")) multiplexer_5 (
    .in0(ID_EX_reg_d2_2), .in1(EX_MEME_alu_out_2), .out(multiplexer_5_out), .sel(forward_unit_1_fwd_dm));
  Adder #(.width(32)) adder_2 (.a(E_PCplus4), .b(shifter_1_out), .out(adder_2_out));  // open: cin, cout
  Shifter #(.width(32)) shifter_1 (.in(E_imm), .\dist (5'b00010), .out(shifter_1_out));
  Multiplexer #(.width(5), .enable("false")) multiplexer_6 (
    .in0(ID_EX_d_addr_2), .in1(ID_EX_t_addr_2), .out(multiplexer_6_out), .sel(ID_EX_ex_cntl_2[0]));
  Forward_Unit forward_unit_1 (
    .S(ID_EX_s_addr_2), .T(ID_EX_t_addr_2),
    .From_the_Mem_this_is_the_Register_Destination(EX_MEME_the_register_in_which_we_will_write__ie__the_destination_2),
    .Mem_Reg_Write(EX_MEME_wb_cntl_2[2]), .The_Output_for_S(forward_unit_1_the_output_for_s),
    .The_Output_for_T(forward_unit_1_the_output_for_t), .WB_Reg_Write(MEM_WB_wb_2[2]),
    .WB_Register_Destination(MEM_WB_register_destination_2), .Clock(Clock), .Fwd_DM(forward_unit_1_fwd_dm));
  EX_MEM EX_MEME (
    .MEM_cntl(ID_EX_mem_cntl_2), .WB_cntl(ID_EX_wb_cntl_2), .Branch_Address(adder_2_out), .Zero(alu_1_zero),
    .ALU_Out(alu_1_aluresult), .The_register_in_which_we_will_write__ie__the_destination(multiplexer_6_out),
    .Mem_Data_to_Write(multiplexer_5_out), .Clock(Clock), .Squash(MEM_Squash),
    .MEM_cntl_2(EX_MEME_mem_cntl_2), .WB_cntl_2(EX_MEME_wb_cntl_2), .Branch_Address_2(Branch_Target),
    .Zero_2(EX_MEME_zero_2), .ALU_Out_2(EX_MEME_alu_out_2),
    .The_register_in_which_we_will_write__ie__the_destination_2(EX_MEME_the_register_in_which_we_will_write__ie__the_destination_2),
    .Mem_Data_to_Write_2(EX_MEME_mem_data_to_write_2), .PC(E_PCplus4), .PC_2(EX_MEME_pc_2));
  and and_1 (and_1_out, EX_MEME_zero_2, EX_MEME_mem_cntl_2[2]);
  RAM #(.dataWidth(32), .bus("separate")) ram_1 (
    .addr(EX_MEME_alu_out_2[7:0]), .din(EX_MEME_mem_data_to_write_2), .data(ram_1_data),
    .str(EX_MEME_mem_cntl_2[1]), .sel(1'b1), .clk(Clock), .ld(EX_MEME_mem_cntl_2[0]));  // open: clr
  MEM_WB MEM_WB (
    .WB(EX_MEME_wb_cntl_2), .Goddamn_RAM_data(ram_1_data), .ALU_OUT(EX_MEME_alu_out_2),
    .Register_Destination(EX_MEME_the_register_in_which_we_will_write__ie__the_destination_2), .Clock(Clock),
    .WB_2(MEM_WB_wb_2), .Goddamn_RAM_data_2(MEM_WB_goddamn_ram_data_2), .ALU_OUT_2(MEM_WB_alu_out_2),
    .Register_Destination_2(MEM_WB_register_destination_2), .Squash(WB_Squash), .PC(EX_MEME_pc_2),
    .PC_2(MEM_WB_pc_2));
  Multiplexer #(.select(2), .width(32), .enable("false")) multiplexer_7 (
    .in0(MEM_WB_goddamn_ram_data_2), .in1(MEM_WB_alu_out_2), .in2(MEM_WB_pc_2), .out(multiplexer_7_out),
    .sel(MEM_WB_wb_2[1:0]));  // open: in3

  // Notes on the sheet:
  //   contents of rom_1 (hex, n*v repeats v):
  //   20010001 5*210820 ac010000 8c020000 211824 ac630000 8c640000 ac640001
endmodule

module _32bit (
  input  Add_Sub_control,
  input  [31:0] in_2,
  input  [31:0] in_3,
  output [31:0] out_4,
  output carry_out
);

  wire adder_1_cout, subtractor_1_bout;
  wire [31:0] adder_1_out, subtractor_1_out;

  Adder #(.width(32)) adder_1 (.a(in_2), .b(in_3), .out(adder_1_out), .cout(adder_1_cout));  // open: cin
  Subtractor #(.width(32)) subtractor_1 (
    .a(in_2), .b(in_3), .out(subtractor_1_out), .bout(subtractor_1_bout));  // open: bin
  Multiplexer #(.width(32), .enable("false")) multiplexer_1 (
    .in0(adder_1_out), .in1(subtractor_1_out), .out(out_4), .sel(Add_Sub_control));
  Multiplexer #(.enable("false")) multiplexer_2 (
    .in0(adder_1_cout), .in1(subtractor_1_bout), .out(carry_out), .sel(Add_Sub_control));
endmodule

module ALU (
  input  [2:0] ALUCtl,
  input  [31:0] A,
  input  [31:0] B,
  input  [4:0] Shamt,
  output [31:0] ALUResult,
  output Zero,
  output Overflow
);

  wire and_2_out, and_3_out, comparator_1_lt, not_1_out, not_2_out, not_3_out, not_4_out, not_5_out, or_2_out;
  wire [31:0] Add, And, LessThan, Nor, Or, ShiftLeft, ShiftRight, Sub, Xor;

  Adder #(.width(32)) adder_1 (.a(A), .b(B), .out(Add));  // open: cin, cout
  Subtractor #(.width(32)) subtractor_1 (.a(A), .b(B), .out(Sub));  // open: bin, bout
  assign And = A & B;  // AND_Gate and_1, 32 bits wide
  assign Or = A | B;  // OR_Gate or_1, 32 bits wide
  assign Nor = ~(A | B);  // NOR_Gate nor_1, 32 bits wide
  Comparator #(.width(32)) comparator_1 (.a(A), .b(B), .lt(comparator_1_lt));  // open: gt, eq
  assign LessThan = {{31{1'b0}}, comparator_1_lt};  // Bit_Extender bit_extender_1
  Shifter #(.width(32)) shifter_1 (.in(B), .\dist (Shamt), .out(ShiftLeft));
  Shifter #(.width(32), .shift("lr")) shifter_2 (.in(B), .\dist (Shamt), .out(ShiftRight));
  not not_1 (not_1_out, ALUCtl[0]);
  not not_2 (not_2_out, ALUCtl[1]);
  not not_3 (not_3_out, ALUCtl[2]);
  not not_4 (not_4_out, ALUCtl[0]);
  not not_5 (not_5_out, ALUCtl[2]);
  and and_2 (and_2_out, not_1_out, not_2_out, not_3_out);
  and and_3 (and_3_out, not_4_out, ALUCtl[1], not_5_out);
  Multiplexer #(.select(3), .width(32), .enable("false")) multiplexer_1 (
    .in0(Sub), .in1(And), .in2(Add), .in3(Or), .in4(LessThan), .in5(ShiftLeft), .in6(ShiftRight), .in7(Xor),
    .out(ALUResult), .sel(ALUCtl));
  Overflow overflow_1 (
    .Add(and_3_out), .Sub(and_2_out), .ASign(A[31]), .BSign(B[31]), .ResultSign(ALUResult[31]),
    .Overflow(Overflow));
  not not_6 (Zero, or_2_out);
  or or_2 (or_2_out, ALUResult[0], ALUResult[1], ALUResult[2], ALUResult[3], ALUResult[4], ALUResult[5], ALUResult[6], ALUResult[7], ALUResult[8], ALUResult[9], ALUResult[10], ALUResult[11], ALUResult[12], ALUResult[13], ALUResult[14], ALUResult[15], ALUResult[16], ALUResult[17], ALUResult[18], ALUResult[19], ALUResult[20], ALUResult[21], ALUResult[22], ALUResult[23], ALUResult[24], ALUResult[25], ALUResult[26], ALUResult[27], ALUResult[28], ALUResult[29], ALUResult[30], ALUResult[31]);

  // Other names for the same wires on the sheet: ASign = A[31]; ResultSign = ALUResult[31]; BSign = B[31]
endmodule

module RegFile (
  input  [4:0] WrAddr,
  input  [31:0] WrData,
  input  WrReg,
  input  [4:0] RdAddr1,
  input  [4:0] RdAddr2,
  input  Clock,
  output [31:0] RdData1,
  output [31:0] RdData2
);

  wire and_1_out, and_2_out, comparator_1_eq, comparator_2_eq, comparator_3_eq, comparator_4_eq, not_1_out,
       not_2_out, WrReg0, WrReg1, WrReg2, WrReg3, WrReg4, WrReg5, WrReg6, WrReg7, WrReg8, WrReg9, WrReg10,
       WrReg11, WrReg12, WrReg13, WrReg14, WrReg15, WrReg16, WrReg17, WrReg18, WrReg19, WrReg20, WrReg21,
       WrReg22, WrReg23, WrReg24, WrReg25, WrReg26, WrReg27, WrReg28, WrReg29, WrReg30, WrReg31;
  wire [31:0] multiplexer_1_out, multiplexer_2_out, RegData1, RegData2, RegData3, RegData4, RegData5,
       RegData6, RegData7, RegData8, RegData9, RegData10, RegData11, RegData12, RegData13, RegData14,
       RegData15, RegData16, RegData17, RegData18, RegData19, RegData20, RegData21, RegData22, RegData23,
       RegData24, RegData25, RegData26, RegData27, RegData28, RegData29, RegData30, RegData31;

  Demultiplexer #(.select(5), .enable("false")) demultiplexer_1 (
    .out0(WrReg0), .out1(WrReg1), .out2(WrReg2), .out3(WrReg3), .out4(WrReg4), .out5(WrReg5), .out6(WrReg6),
    .out7(WrReg7), .out8(WrReg8), .out9(WrReg9), .out10(WrReg10), .out11(WrReg11), .out12(WrReg12),
    .out13(WrReg13), .out14(WrReg14), .out15(WrReg15), .out16(WrReg16), .out17(WrReg17), .out18(WrReg18),
    .out19(WrReg19), .out20(WrReg20), .out21(WrReg21), .out22(WrReg22), .out23(WrReg23), .out24(WrReg24),
    .out25(WrReg25), .out26(WrReg26), .out27(WrReg27), .out28(WrReg28), .out29(WrReg29), .out30(WrReg30),
    .out31(WrReg31), .in(WrReg), .sel(WrAddr));
  Register #(.width(32)) Reg4 (.D(WrData), .en(WrReg4), .Q(RegData4), .clk(Clock));  // open: clr
  Register #(.width(32)) Reg8 (.D(WrData), .en(WrReg8), .Q(RegData8), .clk(Clock));  // open: clr
  Register #(.width(32)) Reg12 (.D(WrData), .en(WrReg12), .Q(RegData12), .clk(Clock));  // open: clr
  Register #(.width(32)) Reg16 (.D(WrData), .en(WrReg16), .Q(RegData16), .clk(Clock));  // open: clr
  Register #(.width(32)) Reg20 (.D(WrData), .en(WrReg20), .Q(RegData20), .clk(Clock));  // open: clr
  Register #(.width(32)) Reg24 (.D(WrData), .en(WrReg24), .Q(RegData24), .clk(Clock));  // open: clr
  Register #(.width(32)) Reg28 (.D(WrData), .en(WrReg28), .Q(RegData28), .clk(Clock));  // open: clr
  Register #(.width(32)) Reg1 (.D(WrData), .en(WrReg1), .Q(RegData1), .clk(Clock));  // open: clr
  Register #(.width(32)) Reg5 (.D(WrData), .en(WrReg5), .Q(RegData5), .clk(Clock));  // open: clr
  Register #(.width(32)) Reg9 (.D(WrData), .en(WrReg9), .Q(RegData9), .clk(Clock));  // open: clr
  Register #(.width(32)) Reg13 (.D(WrData), .en(WrReg13), .Q(RegData13), .clk(Clock));  // open: clr
  Register #(.width(32)) Reg17 (.D(WrData), .en(WrReg17), .Q(RegData17), .clk(Clock));  // open: clr
  Register #(.width(32)) Reg21 (.D(WrData), .en(WrReg21), .Q(RegData21), .clk(Clock));  // open: clr
  Register #(.width(32)) Reg25 (.D(WrData), .en(WrReg25), .Q(RegData25), .clk(Clock));  // open: clr
  Register #(.width(32)) Reg29 (.D(WrData), .en(WrReg29), .Q(RegData29), .clk(Clock));  // open: clr
  Register #(.width(32)) Reg2 (.D(WrData), .en(WrReg2), .Q(RegData2), .clk(Clock));  // open: clr
  Register #(.width(32)) Reg6 (.D(WrData), .en(WrReg6), .Q(RegData6), .clk(Clock));  // open: clr
  Register #(.width(32)) Reg10 (.D(WrData), .en(WrReg10), .Q(RegData10), .clk(Clock));  // open: clr
  Register #(.width(32)) Reg14 (.D(WrData), .en(WrReg14), .Q(RegData14), .clk(Clock));  // open: clr
  Register #(.width(32)) Reg18 (.D(WrData), .en(WrReg18), .Q(RegData18), .clk(Clock));  // open: clr
  Register #(.width(32)) Reg22 (.D(WrData), .en(WrReg22), .Q(RegData22), .clk(Clock));  // open: clr
  Register #(.width(32)) Reg26 (.D(WrData), .en(WrReg26), .Q(RegData26), .clk(Clock));  // open: clr
  Register #(.width(32)) Reg30 (.D(WrData), .en(WrReg30), .Q(RegData30), .clk(Clock));  // open: clr
  Register #(.width(32)) Reg3 (.D(WrData), .en(WrReg3), .Q(RegData3), .clk(Clock));  // open: clr
  Register #(.width(32)) Reg7 (.D(WrData), .en(WrReg7), .Q(RegData7), .clk(Clock));  // open: clr
  Register #(.width(32)) Reg11 (.D(WrData), .en(WrReg11), .Q(RegData11), .clk(Clock));  // open: clr
  Register #(.width(32)) Reg15 (.D(WrData), .en(WrReg15), .Q(RegData15), .clk(Clock));  // open: clr
  Register #(.width(32)) Reg19 (.D(WrData), .en(WrReg19), .Q(RegData19), .clk(Clock));  // open: clr
  Register #(.width(32)) Reg23 (.D(WrData), .en(WrReg23), .Q(RegData23), .clk(Clock));  // open: clr
  Register #(.width(32)) Reg27 (.D(WrData), .en(WrReg27), .Q(RegData27), .clk(Clock));  // open: clr
  Register #(.width(32)) Reg31 (.D(WrData), .en(WrReg31), .Q(RegData31), .clk(Clock));  // open: clr
  Multiplexer #(.select(5), .width(32), .enable("false")) multiplexer_1 (
    .in0({32{1'b0}}), .in1(RegData1), .in2(RegData2), .in3(RegData3), .in4(RegData4), .in5(RegData5),
    .in6(RegData6), .in7(RegData7), .in8(RegData8), .in9(RegData9), .in10(RegData10), .in11(RegData11),
    .in12(RegData12), .in13(RegData13), .in14(RegData14), .in15(RegData15), .in16(RegData16),
    .in17(RegData17), .in18(RegData18), .in19(RegData19), .in20(RegData20), .in21(RegData21),
    .in22(RegData22), .in23(RegData23), .in24(RegData24), .in25(RegData25), .in26(RegData26),
    .in27(RegData27), .in28(RegData28), .in29(RegData29), .in30(RegData30), .in31(RegData31),
    .out(multiplexer_1_out), .sel(RdAddr1));
  Multiplexer #(.select(5), .width(32), .enable("false")) multiplexer_2 (
    .in0({32{1'b0}}), .in1(RegData1), .in2(RegData2), .in3(RegData3), .in4(RegData4), .in5(RegData5),
    .in6(RegData6), .in7(RegData7), .in8(RegData8), .in9(RegData9), .in10(RegData10), .in11(RegData11),
    .in12(RegData12), .in13(RegData13), .in14(RegData14), .in15(RegData15), .in16(RegData16),
    .in17(RegData17), .in18(RegData18), .in19(RegData19), .in20(RegData20), .in21(RegData21),
    .in22(RegData22), .in23(RegData23), .in24(RegData24), .in25(RegData25), .in26(RegData26),
    .in27(RegData27), .in28(RegData28), .in29(RegData29), .in30(RegData30), .in31(RegData31),
    .out(multiplexer_2_out), .sel(RdAddr2));
  Multiplexer #(.width(32), .enable("false")) multiplexer_3 (
    .in0(multiplexer_1_out), .in1(WrData), .out(RdData1), .sel(and_1_out));
  Multiplexer #(.width(32), .enable("false")) multiplexer_4 (
    .in0(multiplexer_2_out), .in1(WrData), .out(RdData2), .sel(and_2_out));
  Comparator #(.width(5), .mode("unsigned")) comparator_1 (
    .a(WrAddr), .b(RdAddr1), .eq(comparator_1_eq));  // open: gt, lt
  and and_1 (and_1_out, comparator_1_eq, WrReg, not_1_out);
  Comparator #(.width(5), .mode("unsigned")) comparator_2 (
    .a(WrAddr), .b(RdAddr2), .eq(comparator_2_eq));  // open: gt, lt
  and and_2 (and_2_out, comparator_2_eq, WrReg, not_2_out);
  Comparator #(.width(5), .mode("unsigned")) comparator_3 (
    .a(WrAddr), .b({5{1'b0}}), .eq(comparator_3_eq));  // open: gt, lt
  not not_1 (not_1_out, comparator_3_eq);
  Comparator #(.width(5), .mode("unsigned")) comparator_4 (
    .a(WrAddr), .b({5{1'b0}}), .eq(comparator_4_eq));  // open: gt, lt
  not not_2 (not_2_out, comparator_4_eq);
endmodule

module Overflow (
  input  Add,
  input  Sub,
  input  ASign,
  input  BSign,
  input  ResultSign,
  output Overflow
);

  wire and_1_out, and_2_out, or_1_out, xnor_1_out, xor_1_out, xor_2_out;

  xnor xnor_1 (xnor_1_out, ASign, BSign);
  xor xor_1 (xor_1_out, ASign, BSign);
  and and_1 (and_1_out, xnor_1_out, Add);
  and and_2 (and_2_out, xor_1_out, Sub);
  or or_1 (or_1_out, and_1_out, and_2_out);
  xor xor_2 (xor_2_out, ResultSign, ASign);
  and and_3 (Overflow, or_1_out, xor_2_out);

  // Notes on the sheet:
  //   Overflow occurs when doing addition and sign(A) == sign(B) && sign(result) != sign(A)
  //   Or
  //   Overflow occurs when doing subtraction and sign(A) != sign(B) && sign(result) != sign(A)
endmodule

module IF_ID (
  input  Clock,
  input  [31:0] PCplus4,
  input  [31:0] Instruction,
  output [31:0] PCplus4_2,
  output [31:0] Instruction_2
);

  Register #(.width(32)) register_1 (.D(PCplus4), .Q(PCplus4_2), .clk(Clock));  // open: en, clr
  Register #(.width(32)) register_2 (.D(Instruction), .Q(Instruction_2), .clk(Clock));  // open: en, clr
endmodule

module ID_EX (
  input  [4:0] S_addr,
  input  [5:0] EX_cntl,
  input  [2:0] MEM_cntl,
  input  [2:0] WB_cntl,
  input  [31:0] PC_plus_4,
  input  [31:0] Reg_D1,
  input  [31:0] Reg_D2,
  input  [31:0] immediate,
  input  [4:0] D_addr,
  input  [4:0] T_addr,
  input  Clock,
  input  Squash,
  input  [4:0] Shamt,
  output [4:0] S_addr_2,
  output [5:0] EX_cntl_2,
  output [2:0] MEM_cntl_2,
  output [2:0] WB_cntl_2,
  output [31:0] PC_plus_4_2,
  output [31:0] Reg_D1_2,
  output [31:0] Reg_D2_2,
  output [31:0] immediate_2,
  output [4:0] D_addr_2,
  output [4:0] T_addr_2,
  output [4:0] Shamt_2
);

  Register #(.width(5)) register_1 (.D(S_addr), .Q(S_addr_2), .clk(Clock), .clr(Squash));  // open: en
  Register #(.width(3)) register_2 (.D(WB_cntl), .Q(WB_cntl_2), .clk(Clock), .clr(Squash));  // open: en
  Register #(.width(32)) register_3 (.D(PC_plus_4), .Q(PC_plus_4_2), .clk(Clock), .clr(Squash));  // open: en
  Register #(.width(32)) register_4 (.D(Reg_D1), .Q(Reg_D1_2), .clk(Clock), .clr(Squash));  // open: en
  Register #(.width(32)) register_5 (.D(Reg_D2), .Q(Reg_D2_2), .clk(Clock), .clr(Squash));  // open: en
  Register #(.width(32)) register_6 (.D(immediate), .Q(immediate_2), .clk(Clock), .clr(Squash));  // open: en
  Register #(.width(5)) register_7 (.D(D_addr), .Q(D_addr_2), .clk(Clock), .clr(Squash));  // open: en
  Register #(.width(5)) register_8 (.D(T_addr), .Q(T_addr_2), .clk(Clock), .clr(Squash));  // open: en
  Register #(.width(5)) register_9 (.D(Shamt), .Q(Shamt_2), .clk(Clock));  // open: en, clr
  Register #(.width(6)) register_10 (.D(EX_cntl), .Q(EX_cntl_2), .clk(Clock), .clr(Squash));  // open: en
  Register #(.width(3)) register_11 (.D(MEM_cntl), .Q(MEM_cntl_2), .clk(Clock), .clr(Squash));  // open: en
endmodule

module Instruction_Splitter (
  input  [31:0] Instruction,
  output [31:0] immediate,
  output [5:0] funct,
  output [4:0] shamt,
  output [4:0] D_reg,
  output [4:0] T_reg,
  output [4:0] S_reg,
  output [5:0] opcode
);

  assign immediate = {{16{Instruction[15]}}, Instruction[15:0]};  // Bit_Extender bit_extender_1

  assign D_reg = Instruction[15:11];
  assign funct = Instruction[5:0];
  assign opcode = Instruction[31:26];
  assign S_reg = Instruction[25:21];
  assign shamt = Instruction[10:6];
  assign T_reg = Instruction[20:16];

  // Notes on the sheet:
  //   I-type
  //   R-type
endmodule

module EX_MEM (
  input  [2:0] MEM_cntl,
  input  [2:0] WB_cntl,
  input  [31:0] Branch_Address,
  input  Zero,
  input  [31:0] ALU_Out,
  input  [4:0] The_register_in_which_we_will_write__ie__the_destination,
  input  [31:0] Mem_Data_to_Write,
  input  Clock,
  input  [31:0] PC,
  input  Squash,
  output [2:0] MEM_cntl_2,
  output [2:0] WB_cntl_2,
  output [31:0] Branch_Address_2,
  output Zero_2,
  output [31:0] ALU_Out_2,
  output [4:0] The_register_in_which_we_will_write__ie__the_destination_2,
  output [31:0] Mem_Data_to_Write_2,
  output [31:0] PC_2
);

  Register #(.width(32)) register_1 (
    .D(Mem_Data_to_Write), .Q(Mem_Data_to_Write_2), .clk(Clock), .clr(Squash));  // open: en
  Register #(.width(3)) register_2 (.D(MEM_cntl), .Q(MEM_cntl_2), .clk(Clock), .clr(Squash));  // open: en
  Register #(.width(3)) register_3 (.D(WB_cntl), .Q(WB_cntl_2), .clk(Clock), .clr(Squash));  // open: en
  Register #(.width(32)) register_4 (.D(Branch_Address), .Q(Branch_Address_2), .clk(Clock), .clr(Squash));  // open: en
  Register #(.width(1)) register_5 (.D(Zero), .Q(Zero_2), .clk(Clock), .clr(Squash));  // open: en
  Register #(.width(32)) register_6 (.D(ALU_Out), .Q(ALU_Out_2), .clk(Clock), .clr(Squash));  // open: en
  Register #(.width(5)) register_7 (
    .D(The_register_in_which_we_will_write__ie__the_destination),
    .Q(The_register_in_which_we_will_write__ie__the_destination_2), .clk(Clock), .clr(Squash));  // open: en
  Register #(.width(32)) register_8 (.D(PC), .Q(PC_2), .clk(Clock), .clr(Squash));  // open: en

  // Other names for the same wires on the sheet: Sqaunch = Squash
endmodule

module MEM_WB (
  input  [2:0] WB,
  input  [31:0] Goddamn_RAM_data,
  input  [31:0] ALU_OUT,
  input  [4:0] Register_Destination,
  input  Clock,
  input  Squash,
  input  [31:0] PC,
  output [2:0] WB_2,
  output [31:0] Goddamn_RAM_data_2,
  output [31:0] ALU_OUT_2,
  output [4:0] Register_Destination_2,
  output [31:0] PC_2
);

  Register #(.width(32)) register_1 (
    .D(Goddamn_RAM_data), .Q(Goddamn_RAM_data_2), .clk(Clock), .clr(Squash));  // open: en
  Register #(.width(32)) register_2 (.D(ALU_OUT), .Q(ALU_OUT_2), .clk(Clock), .clr(Squash));  // open: en
  Register #(.width(5)) register_3 (
    .D(Register_Destination), .Q(Register_Destination_2), .clk(Clock), .clr(Squash));  // open: en
  Register #(.width(32)) register_4 (.D(PC), .Q(PC_2), .clk(Clock), .clr(Squash));  // open: en
  Register #(.width(3)) register_5 (.D(WB), .Q(WB_2), .clk(Clock), .clr(Squash));  // open: en
endmodule

module control (
  input  [5:0] Funct,
  input  [5:0] Opcode,
  input  Clock,
  output WB_Squanch,
  output Mem_Squanch,
  output Ex_Squanch,
  output [2:0] WB,
  output [2:0] Mem,
  output [5:0] Ex
);

  wire undriven;

  ROM #(.addrWidth(12), .dataWidth(15)) rom_1 (
    .addr({Opcode, Funct}), .data({Ex, Mem, WB, Ex_Squanch, Mem_Squanch, WB_Squanch}), .sel(undriven));

  // Notes on the sheet:
  //   contents of rom_1 (hex, n*v repeats v):
  //   5428 28 6428 5*28 8 23*28 2028 28 28 28 1028 3028 4*28 4028 85*28 64*8 64*30 64*108 192*28 64*2a28
  //   64*28 64*4a28 64*28 64*1a28 64*3a28 1344*28 64*2a60 448*28 64*2888 1279*28
endmodule

module Forward_Unit (
  input  [4:0] WB_Register_Destination,
  input  [4:0] From_the_Mem_this_is_the_Register_Destination,
  input  [4:0] S,
  input  WB_Reg_Write,
  input  [4:0] T,
  input  Mem_Reg_Write,
  input  Clock,
  output Fwd_DM,
  output [1:0] The_Output_for_S,
  output [1:0] The_Output_for_T
);

  wire and_1_out, and_4_out, d_ff_1_q, d_ff_2_q, nand_1_out, nor_1_out, nor_2_out, nor_3_out, nor_4_out,
       nor_5_out, nor_6_out, not_1_out, not_2_out, or_1_out, or_2_out;
  wire [1:0] and_2_out, multiplexer_1_out;
  wire [1:1] and_6_out;
  wire [4:0] xor_1_out, xor_2_out, xor_3_out, xor_4_out, xor_5_out, xor_6_out;

  assign xor_1_out = {5{1'b0}} ^ S;  // XOR_Gate xor_1, 5 bits wide
  nor nor_1 (nor_1_out, xor_1_out[4], xor_1_out[3], xor_1_out[2], xor_1_out[1], xor_1_out[0]);
  not not_1 (not_1_out, nor_1_out);
  and and_1 (and_1_out, and_2_out[0], and_2_out[1]);
  D_Flip_Flop d_ff_1 (.clk(Clock), .D(and_1_out), .Q(d_ff_1_q));  // open: Qn, preset, en, reset
  assign xor_2_out = S ^ From_the_Mem_this_is_the_Register_Destination;  // XOR_Gate xor_2, 5 bits wide
  nor nor_2 (nor_2_out, xor_2_out[4], xor_2_out[3], xor_2_out[2], xor_2_out[1], xor_2_out[0]);
  and and_2 (and_2_out[0], not_1_out, nor_2_out, Mem_Reg_Write);
  assign xor_3_out = S ^ WB_Register_Destination;  // XOR_Gate xor_3, 5 bits wide
  nor nor_3 (nor_3_out, xor_3_out[4], xor_3_out[3], xor_3_out[2], xor_3_out[1], xor_3_out[0]);
  and and_3 (and_2_out[1], not_1_out, nor_3_out, WB_Reg_Write);
  nand nand_1 (nand_1_out, and_2_out[1], and_2_out[0]);
  Multiplexer #(.width(2), .enable("false")) multiplexer_1 (
    .in0(and_2_out), .in1(2'b01), .out(multiplexer_1_out), .sel(or_1_out));
  or or_1 (or_1_out, d_ff_1_q, and_1_out);
  Multiplexer #(.width(2), .enable("false")) multiplexer_2 (
    .in0(multiplexer_1_out), .in1(and_2_out), .out(The_Output_for_S), .sel(nand_1_out));
  and and_4 (and_4_out, Fwd_DM, and_6_out[1]);
  assign xor_4_out = From_the_Mem_this_is_the_Register_Destination ^ T;  // XOR_Gate xor_4, 5 bits wide
  nor nor_4 (nor_4_out, xor_4_out[4], xor_4_out[3], xor_4_out[2], xor_4_out[1], xor_4_out[0]);
  and and_5 (Fwd_DM, Mem_Reg_Write, nor_4_out, not_2_out);
  D_Flip_Flop d_ff_2 (.clk(Clock), .D(and_4_out), .Q(d_ff_2_q));  // open: Qn, preset, en, reset
  assign xor_5_out = T ^ WB_Register_Destination;  // XOR_Gate xor_5, 5 bits wide
  nor nor_5 (nor_5_out, xor_5_out[4], xor_5_out[3], xor_5_out[2], xor_5_out[1], xor_5_out[0]);
  Multiplexer #(.width(2), .enable("false")) multiplexer_3 (
    .in0({and_6_out[1], Fwd_DM}), .in1(2'b01), .out(The_Output_for_T), .sel(or_2_out));
  or or_2 (or_2_out, d_ff_2_q, and_4_out);
  assign xor_6_out = {5{1'b0}} ^ T;  // XOR_Gate xor_6, 5 bits wide
  nor nor_6 (nor_6_out, xor_6_out[4], xor_6_out[3], xor_6_out[2], xor_6_out[1], xor_6_out[0]);
  not not_2 (not_2_out, nor_6_out);
  and and_6 (and_6_out[1], not_2_out, nor_5_out, WB_Reg_Write);

  // Notes on the sheet:
  //   so dumb
endmodule
